// Logisim project Pyotor_RAM_Controller_1.circ as structural Verilog: 1 circuit, main circuit main
module main (
);

  wire and_1_out, and_2_out, and_3_out, and_5_out, and_6_out, and_8_out, and_10_out, and_11_out, and_12_out,
       and_13_out, and_14_out, and_15_out, and_16_out, and_17_out, and_18_out, and_19_out, and_21_out,
       clock_1_out, clock_2_out, CLRSCR_out, ENABLE_p2, not_1_out, not_2_out, not_3_out, or_3_out, or_5_out,
       VIDEO_MASK_p2, VRAM_RESET_out, WRITE_p2, X_COUNTER_carry, X_RST_out, Y_RST_out;
  wire [6:0] X_COUNTER_q, Y_COUNTER_q;
  wire [7:0] ADDRESS_sw1, ADDRESS_sw9, and_4_out, and_9_out, bit_extender_1_out, bit_extender_2_out,
       DATA_IN_sw1, or_1_out, or_4_out, ram_1_dout, ram_2_dout, rom_1_data;
  wire [15:0] and_7_out, bit_extender_3_out, counter_1_q, or_2_out;
  wire [23:0] rgb_video_1_p6;

  LED led_1 (.in(or_1_out[0]));
  LED led_2 (.in(or_1_out[0]));
  LED led_3 (.in(or_1_out[1]));
  LED led_4 (.in(or_1_out[2]));
  LED led_5 (.in(or_1_out[2]));
  DipSwitch #(.number(16)) ADDRESS (
    .sw1(ADDRESS_sw1[0]), .sw2(ADDRESS_sw1[1]), .sw3(ADDRESS_sw1[2]), .sw4(ADDRESS_sw1[3]),
    .sw5(ADDRESS_sw1[4]), .sw6(ADDRESS_sw1[5]), .sw7(ADDRESS_sw1[6]), .sw8(ADDRESS_sw1[7]),
    .sw9(ADDRESS_sw9[0]), .sw10(ADDRESS_sw9[1]), .sw11(ADDRESS_sw9[2]), .sw12(ADDRESS_sw9[3]),
    .sw13(ADDRESS_sw9[4]), .sw14(ADDRESS_sw9[5]), .sw15(ADDRESS_sw9[6]), .sw16(ADDRESS_sw9[7]));
  // Switch ENABLE: pin names not known; wires that end beside it: 1'b1, ENABLE_p2
  DipSwitch DATA_IN (
    .sw1(DATA_IN_sw1[0]), .sw2(DATA_IN_sw1[1]), .sw3(DATA_IN_sw1[2]), .sw4(DATA_IN_sw1[3]),
    .sw5(DATA_IN_sw1[4]), .sw6(DATA_IN_sw1[5]), .sw7(DATA_IN_sw1[6]), .sw8(DATA_IN_sw1[7]));
  LED led_6 (.in(or_1_out[3]));
  LED led_7 (.in(or_1_out[3]));
  LED led_8 (.in(or_1_out[4]));
  LED led_9 (.in(or_1_out[5]));
  LED led_10 (.in(or_1_out[5]));
  LED led_11 (.in(or_1_out[6]));
  LED led_12 (.in(or_1_out[6]));
  LED led_13 (.in(or_1_out[7]));
  LED led_14 (.in(or_1_out[7]));
  ROM rom_1 (.addr(ADDRESS_sw9), .data(rom_1_data));
  // Switch WRITE: pin names not known; wires that end beside it: 1'b1, WRITE_p2
  assign or_1_out = DATA_IN_sw1 | or_4_out;  // OR_Gate or_1, 8 bits wide
  Pull_Resistor pull_resistor_1 (.node(WRITE_p2));
  Pull_Resistor pull_resistor_2 (.node(ENABLE_p2));
  // Switch VIDEO_MASK: pin names not known; wires that end beside it: 1'b1, VIDEO_MASK_p2, rom_1_data[1], rom_1_data[2], rom_1_data[3], rom_1_data[4], rom_1_data[5], rom_1_data[6], rom_1_data[7]
  Pull_Resistor pull_resistor_3 (.node(VIDEO_MASK_p2));
  not not_1 (not_1_out, VIDEO_MASK_p2);
  and and_1 (and_1_out, rom_1_data[0], not_1_out);
  Clock #(.highDuration(300), .lowDuration(300)) clock_1 (.out(clock_1_out));
  and and_2 (and_2_out, and_1_out, WRITE_p2);
  and and_3 (and_3_out, and_1_out, ENABLE_p2);
  RAM #(.addrWidth(16)) ram_1 (
    .addr({ADDRESS_sw9, ADDRESS_sw1}), .we(and_2_out), .oe(and_3_out), .clk(clock_1_out), .din(DATA_IN_sw1),
    .dout(ram_1_dout));
  assign bit_extender_1_out = {{7{and_3_out}}, and_3_out};  // Bit_Extender bit_extender_1
  assign and_4_out = bit_extender_1_out & ram_1_dout;  // AND_Gate and_4, 8 bits wide
  assign or_2_out = {ADDRESS_sw9, ADDRESS_sw1} | and_7_out;  // OR_Gate or_2, 16 bits wide
  and and_5 (and_5_out, VIDEO_MASK_p2, WRITE_p2);
  and and_6 (and_6_out, VIDEO_MASK_p2, ENABLE_p2);
  or or_3 (or_3_out, and_6_out, not_2_out);
  not not_2 (not_2_out, clock_1_out);
  assign or_4_out = and_4_out | and_9_out;  // OR_Gate or_4, 8 bits wide
  Clock clock_2 (.out(clock_2_out));
  not not_3 (not_3_out, clock_1_out);
  assign and_7_out = bit_extender_3_out & counter_1_q;  // AND_Gate and_7, 16 bits wide
  RAM #(.addrWidth(16)) ram_2 (
    .addr(or_2_out), .we(and_5_out), .oe(or_3_out), .clk(clock_1_out), .din(DATA_IN_sw1), .dout(ram_2_dout));
  and and_8 (and_8_out, clock_2_out, not_3_out);
  assign bit_extender_2_out = {{7{and_6_out}}, and_6_out};  // Bit_Extender bit_extender_2
  Counter #(.max('hffff), .width(16)) counter_1 (
    .Q(counter_1_q), .clk(and_8_out), .clr(or_5_out));  // open: load, D, count, carry, up
  assign bit_extender_3_out = {{15{and_8_out}}, and_8_out};  // Bit_Extender bit_extender_3
  assign and_9_out = bit_extender_2_out & ram_2_dout;  // AND_Gate and_9, 8 bits wide
  Button VRAM_RESET (.out(VRAM_RESET_out));
  and and_10 (and_10_out, counter_1_q[7], 1'b1);
  and and_11 (and_11_out, counter_1_q[8], 1'b0);
  and and_12 (and_12_out, counter_1_q[9], 1'b1);
  and and_13 (and_13_out, counter_1_q[10], 1'b1);
  and and_14 (and_14_out, counter_1_q[11], 1'b1);
  and and_15 (and_15_out, counter_1_q[12], 1'b1);
  and and_16 (and_16_out, counter_1_q[13], 1'b1);
  Button Y_RST (.out(Y_RST_out));
  Counter #(.max('h7f), .width(7)) Y_COUNTER (
    .count(X_COUNTER_carry), .Q(Y_COUNTER_q), .clk(and_8_out), .clr(Y_RST_out));  // open: load, D, carry, up
  and and_17 (and_17_out, and_10_out, and_11_out);
  and and_18 (and_18_out, and_12_out, and_13_out);
  Button CLRSCR (.out(CLRSCR_out));
  Button X_RST (.out(X_RST_out));
  Counter #(.max('h7f), .width(7)) X_COUNTER (
    .count(1'b1), .Q(X_COUNTER_q), .carry(X_COUNTER_carry), .clk(and_8_out), .clr(X_RST_out));  // open: load, D, up
  and and_19 (and_19_out, and_17_out, and_18_out);
  // AND_Gate and_20 has open pins: in0=and_14_out, in1=and_15_out, out=open
  and and_21 (and_21_out, and_19_out, and_16_out);
  // RGB_Video rgb_video_1: pin names not known; wires that end beside it: CLRSCR_out, and_8_out, and_8_out, X_COUNTER_q, Y_COUNTER_q, rgb_video_1_p6
  or or_5 (or_5_out, and_21_out, VRAM_RESET_out);
  Bit_Extender #(.out_width(24), .\type ("input")) bit_extender_4 (
    .in(ram_2_dout), .out(rgb_video_1_p6));  // open: extend

  // Notes on the sheet:
  //   contents of rom_1 (hex, n*v repeats v):
  //   1 1
endmodule
